// Logisim project ex2.circ as structural Verilog: 1 circuit, main circuit compute_BrUn
module compute_BrUn (
  input  [31:0] INSTRUCTION,
  output BrUn
);

  Comparator #(.mode("unsigned"), .width(1)) comparator_1 (.a(INSTRUCTION[13]), .b(1'b1), .eq(BrUn));  // open: gt, lt
endmodule
